# Fritzing sketch recepteur (saved by Fritzing 0.9.2b)

parts:
  Composant1 = Arduino Uno (Rev3)
  U3 = ENC28J60 [package=ssop28db]
  RF_Link_Receiver_-_433MHz = RF-LINK_TX [package=rf-link_tx]

nets:
  N1: Composant1.D8, U3.CS
  N2: Composant1.D11_PWM/MOSI, U3.SI
  N3: Composant1.D12/MISO, U3.SO
  N4: Composant1.D13/SCK, U3.SCK
  GND: Composant1.GND, U3.TPIN+, RF_Link_Receiver_-_433MHz.GND
  N5: Composant1.D3_PWM, RF_Link_Receiver_-_433MHz.DATA
  5V: Composant1.5V, RF_Link_Receiver_-_433MHz.+5V
